# Fritzing sketch basic-heart-rate-sensor-pcb (saved by Fritzing 1.0.8)
circuit board: 17.272cm x 5.842cm
breadboards: 1

parts:
  R1 = Resistor [tolerance=±5% resistance=220 power=0.25W package=THT]
  J1 = Piezo Speaker  # not connected
  S1 = Pushbutton [package="[THT]"]
  R2 = Trimmer Potentiometer [maximum_resistance=10kΩ knob_status=50% power=0.5W package=THT]
  LCD1 = LCD screen
  R3 = Resistor [tolerance=±5% resistance=220 power=0.25W package=THT]
  R4 = Resistor [tolerance=±5% resistance=220 power=0.25W package=THT]
  S2 = Toggle Switch [package=THT]  # not connected
  S3 = Toggle Switch [package=THT]  # not connected
  part = Photocell (LDR) [power=0.25W dark_resistance_@0.01lx=300kΩ light_resistance_@100lx=400Ω luminance=10lx package=THT]  # not connected
  part_2 = NPN-Transistor [package="TO92 [THT]"]  # not connected
  part_3 = LED - 5mm [color="Red (633nm)" current=0.030A package="5 mm [THT]"]  # not connected
  part_4 = LED - 5mm [color="Red (633nm)" current=0.030A package="5 mm [THT]"]  # not connected
  part_5 = Arduino Uno (Rev3)  # not connected
  part_6 = Arduino Uno (Rev3)  # not connected

nets:
  N1: R1.Pin_0, S1.Pin_1, S1.Pin_2, LCD1.LED+, R4.Pin_0
  N2: S1.Pin_3, S1.Pin_4, R3.Pin_1
  N3: R2.leg1, R2.leg2, LCD1.LED-, R3.Pin_0
